// Logisim project procesor.circ as structural Verilog: 14 circuits, main circuit extender
module extender (
  input  [15:0] imm,
  input  op,
  output [31:0] R
);

  and and_1 (R[31], imm[15], op);

  assign R[30:0] = {{15{R[31]}}, imm};
endmodule

module procesor (
  input  in_1,
  input  in_2
);

  wire incrementer_1_p3, mainctrl_1_alusrc, mainctrl_1_beq, mainctrl_1_bne, mainctrl_1_extopt, mainctrl_1_j,
       mainctrl_1_memread, mainctrl_1_memtoreg, mainctrl_1_memwrite, mainctrl_1_regwrite,
       mipsprogramrom_1_p2, nextpc_1_pcsrc, registerfile_1_p7, zero_1_zero;
  wire [1:0] incrementer_1_p4;
  wire [3:0] mips_alu_1_p3;
  wire [4:0] mipsprogramrom_1_p1_2, multiplexer_2_out;
  wire [29:0] incrementer_1_p1, incrementer_1_p2, nextpc_1_newaddr;
  wire [31:0] extender_1_r, mips_alu_1_p5, mips_ram_1_p6, mipsprogramrom_1_p1, multiplexer_3_out,
       registerfile_1_p1, registerfile_1_p8;
  wire [31:2] multiplexer_1_out;

  Multiplexer #(.width(30), .enable("false")) multiplexer_1 (
    .in0(incrementer_1_p2), .in1(nextpc_1_newaddr), .out(multiplexer_1_out), .sel(nextpc_1_pcsrc));
  // Incrementer #(.width(30)) incrementer_1: pin names not known; wires that end beside it: incrementer_1_p1, incrementer_1_p2, incrementer_1_p3, {incrementer_1_p1, incrementer_1_p4}
  Clock clock_1 (.out(incrementer_1_p3));
  Register #(.width(32)) register_1 (
    .D({multiplexer_1_out, 2'b00}), .en(in_1), .clk(incrementer_1_p3),
    .Q({incrementer_1_p1, incrementer_1_p4}), .clr(in_2));
  // MIPSProgramROM mipsprogramrom_1: pin names not known; wires that end beside it: {mipsprogramrom_1_p1[31:11], mipsprogramrom_1_p1_2, mipsprogramrom_1_p1[5:0]}, mipsprogramrom_1_p2
  extender extender_1 (
    .imm({mipsprogramrom_1_p1[15:11], mipsprogramrom_1_p1_2, mipsprogramrom_1_p1[5:0]}),
    .op(mainctrl_1_extopt), .R(extender_1_r));
  Multiplexer #(.width(5), .enable("false")) multiplexer_2 (
    .in0(mipsprogramrom_1_p1[20:16]), .in1(mipsprogramrom_1_p1[15:11]), .out(multiplexer_2_out),
    .sel(mipsprogramrom_1_p2));
  mainctrl mainctrl_1 (
    .in_1(mipsprogramrom_1_p1[31:26]), .RegDest(mipsprogramrom_1_p2), .RegWrite(mainctrl_1_regwrite),
    .ExtOpt(mainctrl_1_extopt), .ALUSrc(mainctrl_1_alusrc), .Beq(mainctrl_1_beq), .Bne(mainctrl_1_bne),
    .J(mainctrl_1_j), .MemRead(mainctrl_1_memread), .MemWrite(mainctrl_1_memwrite),
    .MemtoReg(mainctrl_1_memtoreg));
  zero zero_1 (.check(mips_alu_1_p5), .zero(zero_1_zero));
  // RegisterFile registerfile_1: pin names not known; wires that end beside it: registerfile_1_p1, incrementer_1_p3, mainctrl_1_regwrite, multiplexer_2_out, mipsprogramrom_1_p1[25:21], mipsprogramrom_1_p1[20:16], registerfile_1_p7, registerfile_1_p8
  Multiplexer #(.width(32), .enable("false")) multiplexer_3 (
    .in0(registerfile_1_p8), .in1(extender_1_r), .out(multiplexer_3_out), .sel(mainctrl_1_alusrc));
  // Mips_ALU mips_alu_1: pin names not known; wires that end beside it: registerfile_1_p7, multiplexer_3_out, mips_alu_1_p3, mipsprogramrom_1_p1_2, mips_alu_1_p5
  nextpc nextpc_1 (
    .PC(incrementer_1_p2), .Beq(mainctrl_1_beq), .Bne(mainctrl_1_bne),
    .imm26({mipsprogramrom_1_p1[25:11], mipsprogramrom_1_p1_2, mipsprogramrom_1_p1[5:0]}), .j(mainctrl_1_j),
    .Zero(zero_1_zero), .Pcsrc(nextpc_1_pcsrc), .Newaddr(nextpc_1_newaddr));
  aluctrl aluctrl_1 (.func(mipsprogramrom_1_p1[5:0]), .opcode(mipsprogramrom_1_p1[31:26]), .out_3(mips_alu_1_p3));
  Multiplexer #(.width(32), .enable("false")) multiplexer_4 (
    .in0(mips_alu_1_p5), .in1(mips_ram_1_p6), .out(registerfile_1_p1), .sel(mainctrl_1_memtoreg));
  // MIPS_RAM #(.addrWidth(24)) mips_ram_1: pin names not known; wires that end beside it: mips_alu_1_p5[23:0], registerfile_1_p8, mainctrl_1_memwrite, incrementer_1_p3, mainctrl_1_memread, mips_ram_1_p6

  // Notes on the sheet:
  //   contents of mipsprogramrom_1 (hex, n*v repeats v):
  //   bne $t0,$t0,prvi addiu $t1,$0,1 addiu $t2,$0,4 prvi: bne $t0,$0,drugi addiu $t0,$t0,2 drugi: ori
  //   $t2,$t0,2 addiu $t1,$0,1 addiu $t2,$0,4 beq $0,$0,treci addiu $t1,$0,1 addiu $t2,$0,4 treci: j prvi
  //   func
  //   sha
  //   rd
  //   rt
  //   rs
  //   opcode
endmodule

module mainctrl (
  input  [5:0] in_1,
  output RegDest,
  output RegWrite,
  output ExtOpt,
  output ALUSrc,
  output Beq,
  output Bne,
  output J,
  output MemRead,
  output MemWrite,
  output MemtoReg
);

  wire and_1_out, and_2_out, and_3_out, and_4_out, and_5_out, and_6_out, and_7_out, and_8_out, and_9_out,
       and_10_out, and_11_out, and_12_out, and_13_out, and_14_out, and_15_out, and_16_out, and_17_out,
       and_18_out, and_19_out, and_20_out, and_21_out, and_22_out, and_23_out, and_24_out, and_25_out,
       and_26_out, and_27_out, and_28_out, and_29_out, and_30_out, and_31_out, and_32_out, and_33_out,
       and_34_out, and_35_out, and_36_out, not_1_out, not_2_out, not_3_out, not_4_out, not_5_out, not_6_out,
       not_7_out, not_8_out, not_9_out, not_10_out, not_11_out, not_12_out, not_13_out, not_14_out,
       not_15_out, not_16_out, not_17_out, not_18_out, not_19_out, not_20_out, not_21_out, not_22_out,
       not_23_out, not_24_out, not_25_out, not_26_out, not_27_out, not_28_out, not_29_out, not_30_out,
       not_31_out, not_32_out, not_33_out, not_34_out, not_35_out, not_36_out, not_37_out, not_38_out,
       not_39_out, not_40_out, not_41_out, not_42_out, not_43_out, not_44_out, not_45_out, not_46_out,
       not_47_out, not_48_out, not_49_out, not_50_out, not_51_out, not_52_out, not_53_out, not_54_out,
       not_55_out, not_56_out, not_57_out, not_58_out, not_59_out, not_60_out, not_61_out, not_62_out,
       not_63_out, not_64_out, not_65_out, not_66_out, not_67_out, not_68_out, not_69_out, not_70_out,
       not_71_out, not_72_out, not_73_out, not_74_out, not_75_out, not_76_out, not_77_out, not_78_out;

  not not_1 (not_1_out, in_1[5]);
  not not_2 (not_2_out, in_1[4]);
  not not_3 (not_3_out, in_1[3]);
  not not_4 (not_4_out, in_1[1]);
  not not_5 (not_5_out, in_1[5]);
  not not_6 (not_6_out, in_1[3]);
  not not_7 (not_7_out, in_1[2]);
  not not_8 (not_8_out, in_1[3]);
  not not_9 (not_9_out, in_1[2]);
  not not_10 (not_10_out, in_1[1]);
  not not_11 (not_11_out, in_1[3]);
  not not_12 (not_12_out, in_1[2]);
  not not_13 (not_13_out, in_1[0]);
  not not_14 (not_14_out, in_1[3]);
  not not_15 (not_15_out, in_1[2]);
  not not_16 (not_16_out, in_1[2]);
  not not_17 (not_17_out, in_1[1]);
  not not_18 (not_18_out, in_1[0]);
  not not_19 (not_19_out, in_1[5]);
  not not_20 (not_20_out, in_1[4]);
  not not_21 (not_21_out, in_1[4]);
  not not_22 (not_22_out, in_1[1]);
  not not_23 (not_23_out, in_1[4]);
  not not_24 (not_24_out, in_1[0]);
  not not_25 (not_25_out, in_1[4]);
  not not_26 (not_26_out, in_1[3]);
  not not_27 (not_27_out, in_1[1]);
  not not_28 (not_28_out, in_1[0]);
  not not_29 (not_29_out, in_1[1]);
  not not_30 (not_30_out, in_1[0]);
  not not_31 (not_31_out, in_1[3]);
  not not_32 (not_32_out, in_1[2]);
  not not_33 (not_33_out, in_1[2]);
  not not_34 (not_34_out, in_1[0]);
  not not_35 (not_35_out, in_1[0]);
  not not_36 (not_36_out, in_1[5]);
  not not_37 (not_37_out, in_1[4]);
  not not_38 (not_38_out, in_1[3]);
  not not_39 (not_39_out, in_1[1]);
  not not_40 (not_40_out, in_1[0]);
  not not_41 (not_41_out, in_1[0]);
  not not_42 (not_42_out, in_1[4]);
  not not_43 (not_43_out, in_1[2]);
  or or_1 (ALUSrc, in_1[1], in_1[3]);
  not not_44 (not_44_out, in_1[5]);
  not not_45 (not_45_out, in_1[3]);
  not not_46 (not_46_out, in_1[2]);
  not not_47 (not_47_out, in_1[3]);
  not not_48 (not_48_out, in_1[2]);
  not not_49 (not_49_out, in_1[1]);
  not not_50 (not_50_out, in_1[5]);
  not not_51 (not_51_out, in_1[4]);
  not not_52 (not_52_out, in_1[3]);
  not not_53 (not_53_out, in_1[1]);
  not not_54 (not_54_out, in_1[0]);
  not not_55 (not_55_out, in_1[3]);
  not not_56 (not_56_out, in_1[2]);
  not not_57 (not_57_out, in_1[3]);
  not not_58 (not_58_out, in_1[1]);
  not not_59 (not_59_out, in_1[3]);
  not not_60 (not_60_out, in_1[1]);
  not not_61 (not_61_out, in_1[3]);
  not not_62 (not_62_out, in_1[1]);
  not not_63 (not_63_out, in_1[5]);
  not not_64 (not_64_out, in_1[3]);
  not not_65 (not_65_out, in_1[2]);
  not not_66 (not_66_out, in_1[3]);
  not not_67 (not_67_out, in_1[2]);
  not not_68 (not_68_out, in_1[0]);
  not not_69 (not_69_out, in_1[3]);
  not not_70 (not_70_out, in_1[2]);
  not not_71 (not_71_out, in_1[3]);
  not not_72 (not_72_out, in_1[3]);
  not not_73 (not_73_out, in_1[2]);
  not not_74 (not_74_out, in_1[2]);
  not not_75 (not_75_out, in_1[5]);
  not not_76 (not_76_out, in_1[3]);
  not not_77 (not_77_out, in_1[1]);
  not not_78 (not_78_out, in_1[2]);
  and and_1 (and_1_out, not_1_out, not_2_out, not_3_out, not_4_out);
  and and_2 (and_2_out, not_5_out, not_6_out, not_7_out);
  and and_3 (and_3_out, not_8_out, not_9_out, not_10_out);
  and and_4 (and_4_out, not_11_out, not_12_out, not_13_out);
  and and_5 (and_5_out, in_1[4], not_14_out, not_15_out);
  and and_6 (and_6_out, not_16_out, not_17_out, not_18_out);
  and and_7 (and_7_out, not_19_out, not_20_out, in_1[3]);
  and and_8 (and_8_out, not_21_out, in_1[3], not_22_out);
  and and_9 (and_9_out, not_23_out, in_1[3], not_24_out);
  and and_10 (and_10_out, not_25_out, in_1[3], in_1[2]);
  and and_11 (and_11_out, in_1[4], not_26_out);
  and and_12 (and_12_out, in_1[4], not_27_out, not_28_out);
  and and_13 (and_13_out, in_1[5], not_29_out, not_30_out);
  and and_14 (and_14_out, in_1[5], not_31_out, not_32_out, in_1[1], in_1[0]);
  and and_15 (and_15_out, not_33_out, not_34_out);
  and and_16 (and_16_out, in_1[1], not_35_out);
  and and_17 (and_17_out, not_36_out, not_37_out, not_38_out, in_1[2], not_39_out);
  and and_18 (and_18_out, in_1[4], not_40_out);
  and and_19 (and_19_out, in_1[5], not_41_out);
  and and_20 (and_20_out, in_1[5], not_42_out, not_43_out, in_1[1]);
  and and_21 (and_21_out, not_44_out, not_45_out, not_46_out, in_1[0]);
  and and_22 (and_22_out, not_47_out, not_48_out, not_49_out, in_1[0]);
  and and_23 (and_23_out, not_50_out, not_51_out, not_52_out, in_1[2], not_53_out, not_54_out);
  and and_24 (and_24_out, in_1[4], not_55_out, not_56_out, in_1[0]);
  and and_25 (and_25_out, not_57_out, in_1[2], not_58_out, in_1[0]);
  or or_2 (Bne, and_25_out, and_26_out, and_27_out);
  and and_26 (and_26_out, in_1[4], not_59_out, in_1[2], not_60_out);
  and and_27 (and_27_out, in_1[5], not_61_out, in_1[2], not_62_out);
  and and_28 (and_28_out, not_63_out, not_64_out, not_65_out, in_1[1]);
  or or_3 (J, and_28_out, and_29_out, and_30_out);
  and and_29 (and_29_out, not_66_out, not_67_out, not_68_out, in_1[1]);
  and and_30 (and_30_out, in_1[4], not_69_out, not_70_out, in_1[1]);
  and and_31 (and_31_out, in_1[4], not_71_out);
  or or_4 (MemRead, and_31_out, and_32_out);
  and and_32 (and_32_out, in_1[5], not_72_out, not_73_out, in_1[0], in_1[1]);
  and and_33 (and_33_out, in_1[4], in_1[3]);
  or or_5 (MemWrite, and_33_out, and_34_out);
  and and_34 (and_34_out, in_1[5], in_1[3], not_74_out, in_1[0], in_1[1]);
  and and_35 (and_35_out, not_75_out, not_76_out, in_1[2], not_77_out);
  or or_6 (MemtoReg, and_35_out, in_1[4], and_36_out);
  and and_36 (and_36_out, in_1[5], not_78_out, in_1[1], in_1[0]);
  or or_7 (RegDest, and_1_out, and_2_out, and_3_out, and_4_out, and_5_out);
  or or_8 (RegWrite, and_6_out, and_7_out, and_8_out, and_9_out, and_10_out, and_11_out, and_12_out, and_13_out, and_14_out);
  or or_9 (ExtOpt, and_15_out, and_16_out, and_17_out, and_18_out, and_19_out, and_20_out);
  or or_10 (Beq, and_21_out, and_22_out, and_23_out, and_24_out);
endmodule

module aluctrl (
  input  [5:0] func,
  input  [5:0] opcode,
  output [3:0] out_3
);

  wire nor_1_out;
  wire [3:0] alui_1_o3_2, alur_1_o3;

  aluR alur_1 (
    .f0(func[5]), .f1(func[4]), .f2(func[3]), .f3(func[2]), .f4(func[1]), .f5(func[0]), .o0(alur_1_o3[3]),
    .o1(alur_1_o3[2]), .o2(alur_1_o3[1]), .o3(alur_1_o3[0]));
  nor nor_1 (nor_1_out, opcode[5], opcode[4], opcode[3], opcode[2], opcode[1], opcode[0]);
  alui alui_1 (
    .o0(opcode[5]), .o1(opcode[4]), .o2(opcode[3]), .o3(opcode[2]), .o4(opcode[1]), .o5(opcode[0]),
    .o0_2(alui_1_o3_2[3]), .o1_2(alui_1_o3_2[2]), .o2_2(alui_1_o3_2[1]), .o3_2(alui_1_o3_2[0]));
  Multiplexer #(.width(4), .enable("false")) multiplexer_1 (
    .in0(alui_1_o3_2), .in1(alur_1_o3), .out(out_3), .sel(nor_1_out));
endmodule

module aluR (
  input  f0,
  input  f1,
  input  f2,
  input  f3,
  input  f4,
  input  f5,
  output o0,
  output o1,
  output o2,
  output o3
);

  wire not_1_out;

  and and_1 (o2, f0, f5);
  not not_1 (not_1_out, f0);
  and and_2 (o3, not_1_out, f5);

  assign o0 = f3;
  assign o1 = f4;
endmodule

module nextpc (
  input  [29:0] PC,
  input  Beq,
  input  Bne,
  input  [25:0] imm26,
  input  j,
  input  Zero,
  output Pcsrc,
  output [29:0] Newaddr
);

  wire and_1_out, and_2_out;
  wire [29:0] adder_1_out, bit_extender_1_out;

  assign bit_extender_1_out = {{14{imm26[15]}}, imm26[15:0]};  // Bit_Extender bit_extender_1
  Adder #(.width(30)) adder_1 (.a(PC), .b(bit_extender_1_out), .out(adder_1_out));  // open: cin, cout
  Multiplexer #(.width(30), .enable("false")) multiplexer_1 (
    .in0(adder_1_out), .in1({PC[29:26], imm26}), .out(Newaddr), .sel(j));
  or or_1 (Pcsrc, and_1_out, j, and_2_out);
  and and_1 (and_1_out, ~Zero, Bne);  // AND_Gate
  and and_2 (and_2_out, Zero, Beq);
endmodule

module zero (
  input  [31:0] check,
  output zero
);

  nor nor_1 (zero, check[31], check[30], check[29], check[28], check[27], check[26], check[25], check[24], check[23], check[22], check[21], check[20], check[19], check[18], check[17], check[16], check[15], check[14], check[13], check[12], check[11], check[10], check[9], check[8], check[7], check[6], check[5], check[4], check[3], check[2], check[1], check[0]);
endmodule

module alui (
  input  o0,
  input  o1,
  input  o2,
  input  o3,
  input  o4,
  input  o5,
  output o0_2,
  output o1_2,
  output o2_2,
  output o3_2
);

  wire and_2_out, and_3_out, not_1_out, not_2_out, not_3_out, not_4_out;

  and and_1 (o0_2, o2, o3);
  not not_1 (not_1_out, o2);
  not not_2 (not_2_out, o4);
  not not_3 (not_3_out, o5);
  not not_4 (not_4_out, o2);
  and and_2 (and_2_out, not_1_out, not_2_out);
  and and_3 (and_3_out, o4, not_3_out);
  or or_1 (o2_2, not_4_out, o5);
  or or_2 (o1_2, and_2_out, and_3_out);

  assign o3_2 = 1'b0;
endmodule

module rtip (
  input  in_1,
  input  in_2,
  input  in_3
);

  wire clock_1_out, registerfile_1_p1, registerfile_1_p7, registerfile_1_p8;
  wire [1:0] incrementer_1_p4;
  wire [3:0] mips_alu_1_p3;
  wire [29:0] incrementer_1_p2;
  wire [31:0] mipsprogramrom_1_p1;
  wire [31:2] incrementer_1_p3;

  Clock clock_1 (.out(clock_1_out));
  // Incrementer #(.width(30)) incrementer_1: pin names not known; wires that end beside it: in_2, incrementer_1_p2, incrementer_1_p3, {incrementer_1_p2, incrementer_1_p4}
  Register #(.width(32)) register_1 (
    .D({incrementer_1_p3, 2'b00}), .en(in_2), .clk(clock_1_out), .Q({incrementer_1_p2, incrementer_1_p4}),
    .clr(in_3));
  // MIPSProgramROM mipsprogramrom_1: pin names not known; wires that end beside it: mipsprogramrom_1_p1, mipsprogramrom_1_p1[31:26]
  // RegisterFile registerfile_1: pin names not known; wires that end beside it: registerfile_1_p1, clock_1_out, in_1, mipsprogramrom_1_p1[15:11], mipsprogramrom_1_p1[25:21], mipsprogramrom_1_p1[20:16], registerfile_1_p7, registerfile_1_p8
  // Mips_ALU mips_alu_1: pin names not known; wires that end beside it: registerfile_1_p7, registerfile_1_p8, mips_alu_1_p3, mipsprogramrom_1_p1[10:6], registerfile_1_p1
  aluctrl aluctrl_1 (.func(mipsprogramrom_1_p1[5:0]), .out_3(mips_alu_1_p3));  // open: opcode

  // Notes on the sheet:
  //   contents of mipsprogramrom_1 (hex, n*v repeats v):
  //   subu $t3,$t0,$t1 and $t2,$t0,$t1 or $t3,$t0,$t1 xor $t2,$t0,$t1 nor $t4,$t0,$t1 sll $t2,$t0,4 srl
  //   $t3,$t1,1 sra $t4,$t0,2
endmodule

module ader (
  input  a,
  input  b,
  input  cin,
  output o,
  output cout
);

  wire and_1_out, and_2_out, and_3_out, and_4_out, and_5_out, and_6_out, and_7_out, not_1_out, not_2_out,
       not_3_out, not_4_out, not_5_out, not_6_out;

  not not_1 (not_1_out, a);
  not not_2 (not_2_out, b);
  not not_3 (not_3_out, a);
  not not_4 (not_4_out, cin);
  not not_5 (not_5_out, b);
  not not_6 (not_6_out, cin);
  and and_1 (and_1_out, b, cin);
  and and_2 (and_2_out, a, cin);
  and and_3 (and_3_out, a, b);
  and and_4 (and_4_out, not_1_out, not_2_out, cin);
  and and_5 (and_5_out, not_3_out, b, not_4_out);
  and and_6 (and_6_out, a, not_5_out, not_6_out);
  and and_7 (and_7_out, a, b, cin);
  or or_1 (cout, and_1_out, and_2_out, and_3_out);
  or or_2 (o, and_4_out, and_5_out, and_6_out, and_7_out);
endmodule

module alologic (
  input  [1:0] a,
  input  [1:0] b,
  input  [1:0] op,
  output [1:0] R
);

  wire [1:0] and_1_out, nor_1_out, or_1_out, xor_1_out;

  assign and_1_out = a & b;  // AND_Gate and_1, 2 bits wide
  assign or_1_out = a | b;  // OR_Gate or_1, 2 bits wide
  assign nor_1_out = ~(a | b);  // NOR_Gate nor_1, 2 bits wide
  assign xor_1_out = a ^ b;  // XOR_Gate xor_1, 2 bits wide
  Multiplexer #(.select(2), .width(2), .enable("false")) multiplexer_1 (
    .in0(and_1_out), .in1(or_1_out), .in2(nor_1_out), .in3(xor_1_out), .out(R), .sel(op));
endmodule

module adder2 (
  input  cin,
  input  [1:0] a,
  input  [1:0] b,
  output [1:0] out_4,
  output cout
);

  wire ader_1_cout;

  ader ader_1 (.a(a[0]), .b(b[0]), .cin(cin), .o(out_4[0]), .cout(ader_1_cout));
  ader ader_2 (.a(a[1]), .b(b[1]), .cin(ader_1_cout), .o(out_4[1]), .cout(cout));
endmodule

module addsub (
  input  op,
  input  [1:0] a,
  input  [1:0] b,
  output [1:0] R,
  output cout
);

  wire [1:0] xor_1_out;

  assign xor_1_out = b ^ {2{op}};  // XOR_Gate xor_1, 2 bits wide
  adder2 adder2_1 (.cin(op), .a(a), .b(xor_1_out), .out_4(R), .cout(cout));
endmodule

module alu (
  input  [1:0] in_1,
  input  [1:0] in_2
);

  wire undriven;

  addsub addsub_1 (.op(undriven), .a(in_1), .b(in_2));  // open: R, cout
  alologic alologic_1 (.a(in_1));  // open: b, op, R
endmodule
